# Fritzing sketch BlindController3-CircuitBoard (saved by Fritzing 0.8.3b)

parts:
  U1 = RELAY [package=relay-jzc]
  U2 = RELAY [package=relay-jzc]
  U3 = RELAY [package=relay-jzc]
  U4 = RELAY [package=relay-jzc]
  Part1 = Spark Core (v1.0)
  M1 = DC Motor
  Power_plug1 = Power plug
  Part2 = HX711 Weighing Sensor Module
  Part3 = HX711 Weighing Sensor Module
  J1 = LOAD_CELL [package=1x03]
  U5 = mystery part, 24 pins [chip_label="Wheatstone bridge"]
  J3 = LOAD_CELL [package=1x03]
  J4 = LOAD_CELL [package=1x03]
  J5 = LOAD_CELL [package=1x03]
  J6 = LOAD_CELL [package=1x03]
  J7 = LOAD_CELL [package=1x03]
  J8 = LOAD_CELL [package=1x03]
  J9 = LOAD_CELL [package=1x03]
  U6 = mystery part, 24 pins [chip_label="Wheatstone bridge"]
  U9 = mystery part, 3 pins [chip_label=3v3]
  U8 = mystery part, 3 pins [chip_label=GND]
  U7 = mystery part, 5 pins [chip_label=GND]
  M2 = DC Motor

nets:
  N1: U1.COIL2, U2.COIL2, U3.COIL2, U4.COIL2, Power_plug1.VCC
  N2: U1.NC, M1.pin_2
  N3: U1.NO, U2.NO, U3.NO, U4.NO, Power_plug1.GND
  N4: U1.MAIN, Part1.A3
  N5: U1.COIL1, U7.pin1
  N6: U2.NC, M1.pin_1
  N7: U2.MAIN, Part1.A2
  N8: U2.COIL1, U7.pin2
  N9: U3.NC, M2.pin_2
  N10: U3.MAIN, Part1.A1
  N11: U3.COIL1, U7.pin3
  N12: U4.NC, M2.pin_1
  N13: U4.MAIN, Part1.A0
  N14: U4.COIL1, U7.pin4
  N15: Part1.GND, U8.pin1, U7.pin5
  N16: Part1.D1, Part3.DO/RX
  N17: Part1.D2, Part3.CK/TX
  N18: Part1.D6, Part2.DO/RX
  N19: Part1.D7, Part2.CK/TX
  N20: Part1.3V3*, U9.pin1
  N21: Part2.VCC, U8.pin3
  N22: Part2.GND, U9.pin3
  N23: Part2.A+, U6.pin24
  N24: Part2.A-, U6.pin23
  N25: Part2.B+, U6.pin22
  N26: Part2.B-, U6.pin21
  N27: Part3.VCC, U8.pin2
  N28: Part3.GND, U9.pin2
  N29: Part3.A+, U5.pin24
  N30: Part3.A-, U5.pin23
  N31: Part3.B+, U5.pin22
  N32: Part3.B-, U5.pin21
  N33: J1.B, U5.pin1
  N34: J1.W, U5.pin2
  N35: J1.R, U5.pin3
  N36: U5.pin4, J3.B
  N37: U5.pin5, J3.W
  N38: U5.pin6, J3.R
  N39: U5.pin7, J4.B
  N40: U5.pin8, J4.W
  N41: U5.pin9, J4.R
  N42: U5.pin10, J5.B
  N43: U5.pin11, J5.W
  N44: U5.pin12, J5.R
  N45: J6.B, U6.pin1
  N46: J6.W, U6.pin2
  N47: J6.R, U6.pin3
  N48: J7.B, U6.pin4
  N49: J7.W, U6.pin5
  N50: J7.R, U6.pin6
  N51: J8.B, U6.pin7
  N52: J8.W, U6.pin8
  N53: J8.R, U6.pin9
  N54: J9.B, U6.pin10
  N55: J9.W, U6.pin11
  N56: J9.R, U6.pin12

notes:
  2 sets of 4x strain gauges
  double throw relays
  blind motors
  Microcontroller
  HX711 load cell amplifiers
  12V Power
